// Logisim project Exercicio2Jogadores4bits.circ as structural Verilog: 1 circuit, main circuit main
module main (
  input  [3:0] in_1,
  input  [3:0] in_2,
  input  in_3,
  input  [3:0] \Nº_P1 ,
  input  in_5,
  input  [3:0] in_6,
  input  [3:0] in_7,
  input  Clock,
  input  Anti_Clock,
  input  [3:0] in_10,
  input  Clear,
  input  [3:0] in_12,
  input  [3:0] in_13,
  input  [3:0] \Nº_P1_2 ,
  input  [3:0] in_15,
  input  in_16,
  input  [3:0] in_17,
  input  [3:0] in_18,
  output [3:0] \Nº_P1_3 ,
  output out_20,
  output Empate,
  output out_22,
  output out_23,
  output Empate_2,
  output out_25,
  output [3:0] out_26,
  output out_27,
  output Empate_3,
  output out_29
);

  wire comparator_1_eq, comparator_2_eq, comparator_3_eq, comparator_4_eq, comparator_6_eq, comparator_7_eq,
       not_1_out, not_2_out, not_3_out, not_4_out, not_5_out, not_6_out, xor_1_out, xor_2_out;

  Comparator #(.width(4)) comparator_1 (.a(\Nº_P1 ), .b(in_6), .eq(comparator_1_eq));  // open: gt, lt
  Comparator #(.width(4)) comparator_2 (.a(in_10), .b(in_12), .eq(comparator_2_eq));  // open: gt, lt
  Comparator #(.width(4)) comparator_3 (.a(\Nº_P1_2 ), .b(in_15), .eq(comparator_3_eq));  // open: gt, lt
  not not_1 (not_1_out, comparator_4_eq);
  not not_2 (not_2_out, comparator_3_eq);
  Comparator #(.width(4)) comparator_4 (.a(in_17), .b(in_18), .eq(comparator_4_eq));  // open: gt, lt
  Comparator #(.width(1)) comparator_5 (
    .a(comparator_1_eq), .b(comparator_2_eq), .gt(out_23), .eq(Empate_2), .lt(out_25));
  and and_1 (out_27, comparator_3_eq, not_1_out, in_16);
  and and_2 (out_29, in_16, not_2_out, comparator_4_eq);
  xor xor_1 (xor_1_out, comparator_3_eq, comparator_4_eq);
  not not_3 (not_3_out, xor_1_out);
  and and_3 (Empate_3, not_3_out, in_16);
  Register #(.trigger("high"), .width(4)) register_1 (
    .D(in_2), .en(Anti_Clock), .Q(\Nº_P1_3 ), .clk(Clock), .clr(Clear));
  D_Flip_Flop d_ff_1 (.D(in_13[3]), .clk(Clock), .Q(out_26[3]), .preset(in_13[2]), .reset(Clear));  // open: Qn
  D_Flip_Flop d_ff_2 (.D(in_13[2]), .clk(Clock), .Q(out_26[2]), .reset(Clear));  // open: Qn, preset
  Comparator #(.width(4)) comparator_6 (.a(in_1), .b(\Nº_P1_3 ), .eq(comparator_6_eq));  // open: gt, lt
  not not_4 (not_4_out, comparator_7_eq);
  not not_5 (not_5_out, comparator_6_eq);
  Comparator #(.width(4)) comparator_7 (.a(in_7), .b(out_26), .eq(comparator_7_eq));  // open: gt, lt
  D_Flip_Flop d_ff_3 (.D(in_13[1]), .clk(Clock), .Q(out_26[1]), .reset(Clear));  // open: Qn, preset
  and and_4 (out_20, comparator_6_eq, not_4_out, in_5);
  and and_5 (out_22, in_5, not_5_out, comparator_7_eq);
  D_Flip_Flop d_ff_4 (.D(in_13[0]), .clk(Clock), .Q(out_26[0]), .reset(Clear));  // open: Qn, preset
  xor xor_2 (xor_2_out, comparator_6_eq, comparator_7_eq);
  not not_6 (not_6_out, xor_2_out);
  and and_6 (Empate, not_6_out, in_5);

  // Notes on the sheet:
  //   Palpite P2
  //   Nº P2
  //   Palpite P1
  //   Palpite P2
  //   V
  //   Nº P2
  //   Palpite P1
  //   A
  //   B
  //   Player 1 ganha
  //   Player 2 ganha
  //   Clock
  //   Palpite P1
  //   Palpite P2
  //   Player 2 ganha
  //   Player 1 ganha
  //   V
  //   Nº P2
  //   A
  //   B
  //   Register with 4 bits with Flip Flops
  //   Player 2 ganha
  //   Player 1 ganha
endmodule
