// Logisim project ExercicioCaixasCamiao.circ as structural Verilog: 1 circuit, main circuit main
module main (
  input  [3:0] in_1,
  input  [3:0] in_2,
  input  [3:0] in_3,
  input  [3:0] in_4,
  input  [3:0] in_5,
  input  [3:0] in_6,
  input  [3:0] in_7,
  input  [3:0] in_8,
  output out_9,
  output out_10,
  output out_11,
  output out_12,
  output [3:0] out_13,
  output [3:0] out_14,
  output [3:0] out_15,
  output out_16,
  output out_17,
  output out_18,
  output out_19,
  output [3:0] out_20,
  output [3:0] out_21,
  output [3:0] out_22
);

  wire button_1_out, button_2_out, button_3_out, button_4_out, button_5_out, button_6_out, button_7_out,
       button_8_out, button_9_out, comparator_5_eq, comparator_6_eq, nor_1_out, not_1_out, not_2_out,
       not_3_out;

  Button button_1 (.out(button_1_out));
  Button button_2 (.out(button_2_out));
  Button button_3 (.out(button_3_out));
  Button button_4 (.out(button_4_out));
  Counter #(.max('hf), .width(4)) counter_1 (
    .count(not_1_out), .Q(out_14), .clk(button_1_out), .clr(button_2_out));  // open: load, D, carry, up
  not not_1 (not_1_out, out_11);
  Counter #(.max('hf), .width(4)) counter_2 (
    .load(out_17), .D(in_5), .Q(out_20), .clk(button_3_out), .clr(button_4_out));  // open: count, carry, up
  Comparator #(.width(4)) comparator_1 (.a(in_1), .b(out_14), .eq(out_11), .lt(out_12));  // open: gt
  Comparator #(.width(4)) comparator_2 (.a(in_4), .b(out_20), .eq(out_17), .lt(out_19));  // open: gt
  Button button_5 (.out(button_5_out));
  Button button_6 (.out(button_6_out));
  Button button_7 (.out(button_7_out));
  Button button_8 (.out(button_8_out));
  Button button_9 (.out(button_9_out));
  Counter #(.max('hf), .width(4)) counter_3 (
    .count(nor_1_out), .Q(out_15), .clk(button_5_out), .clr(button_6_out));  // open: load, D, carry, up
  nor nor_1 (nor_1_out, out_10, comparator_5_eq);
  Counter #(.max('hf), .width(4)) counter_4 (
    .load(out_18), .D(in_8), .count(not_3_out), .Q(out_22), .clk(button_8_out), .clr(button_9_out));  // open: carry, up
  Comparator #(.width(4)) comparator_3 (.a(in_2), .b(out_15), .eq(out_10), .lt(out_9));  // open: gt
  Comparator #(.width(4)) comparator_4 (.a(in_6), .b(out_22), .eq(out_18), .lt(out_16));  // open: gt
  Counter #(.max('hf), .width(4)) counter_5 (
    .count(not_2_out), .Q(out_13), .clk(out_10), .clr(button_7_out));  // open: load, D, carry, up
  Counter #(.max('hf), .width(4)) counter_6 (
    .count(not_3_out), .Q(out_21), .clk(out_18), .clr(button_9_out));  // open: load, D, carry, up
  Comparator #(.width(4)) comparator_5 (.a(in_3), .b(out_13), .eq(comparator_5_eq));  // open: gt, lt
  not not_2 (not_2_out, comparator_5_eq);
  Comparator #(.width(4)) comparator_6 (.a(in_7), .b(out_21), .eq(comparator_6_eq));  // open: gt, lt
  not not_3 (not_3_out, comparator_6_eq);

  // Notes on the sheet:
  //   Caixa Inicial
  //   Tamanho da Caixa
  //   Add box
  //   Reset
  //   Tamanho da Caixa
  //   Add box
  //   Reset
  //   Caixa Cheia
  //   Caixa Cheia
  //   Caixa por encher
  //   Caixa por encher
  //   Tamanho da Caixa
  //   Add bottle
  //   Reset Caixa
  //   Reset Camião
  //   Tamanho da Caixa
  //   Add bottle
  //   Reset
  //   Caixa por encher
  //   Caixa Cheia
  //   Caixa Cheia
  //   Tamanho do Camião
  //   Caixa por encher
  //   Tamanho do Camião
endmodule
