// Logisim project TestePratico2_Rafa.circ as structural Verilog: 1 circuit, main circuit main
module main (
  input  [1:0] X_Case,
  input  [1:0] in_2,
  input  [1:0] _00___A,
  input  [1:0] OP,
  output [2:0] out_5,
  output [1:0] out_6,
  output [1:0] out_7,
  output [2:0] out_8,
  output [1:0] out_9,
  output [1:0] out_10,
  output [2:0] R,
  output [2:0] out_12,
  output [1:0] out_13
);

  wire and_2_out, and_3_out, clock_1_out, comparator_1_eq, comparator_2_eq, comparator_3_eq, comparator_4_eq,
       comparator_4_gt, comparator_4_lt, not_1_out, not_2_out, or_1_out, or_2_out, random_2_p1;
  wire [1:0] adder_1_out, multiplier_1_out, subtractor_1_out;
  wire [2:0] undriven;

  Random #(.width(2)) random_1 ();  // open: clk, next, out, clr
  // Random #(.width(2)) random_2: pin names not known; wires that end beside it: random_2_p1, random_2_p1
  // Random #(.width(2)) random_3: pin names not known; wires that end beside it: random_2_p1, random_2_p1
  // Random #(.width(3)) random_4: pin names not known; wires that end beside it: random_2_p1
  LED led_1 (.in(random_2_p1));
  Comparator #(.width(2)) comparator_1 (.a(in_2), .b(X_Case), .eq(comparator_1_eq));  // open: gt, lt
  Comparator #(.width(2)) comparator_2 (.a(X_Case), .b(_00___A), .eq(comparator_2_eq));  // open: gt, lt
  Comparator #(.width(2)) comparator_3 (.a(X_Case), .b(OP), .eq(comparator_3_eq));  // open: gt, lt
  Multiplexer #(.enable("true"), .select(2), .width(2)) multiplexer_1 (
    .in0(out_6), .in1(out_9), .in2(out_13), .out(out_7), .sel(in_2));  // open: in3, en
  Clock clock_1 (.out(clock_1_out));
  or or_1 (or_1_out, comparator_1_eq, comparator_3_eq, comparator_2_eq);
  Multiplexer #(.enable("true"), .select(2), .width(2)) multiplexer_2 (
    .in0(out_6), .in1(out_9), .in2(out_13), .out(out_10), .sel(_00___A));  // open: in3, en
  and and_1 (random_2_p1, clock_1_out, not_1_out);
  not not_1 (not_1_out, or_1_out);
  LED led_2 (.in(or_1_out));
  not not_2 (not_2_out, random_2_p1);
  Comparator #(.width(3)) comparator_4 (
    .a(R), .b(undriven), .gt(comparator_4_gt), .eq(comparator_4_eq), .lt(comparator_4_lt));
  and and_2 (and_2_out, not_2_out, comparator_4_eq);
  LED led_3 (.in(and_2_out));
  Adder #(.width(2)) adder_1 (.a(out_7), .b(out_10), .out(adder_1_out));  // open: cin, cout
  Subtractor #(.width(2)) subtractor_1 (.a(out_7), .b(out_10), .out(subtractor_1_out));  // open: bin, bout
  Multiplier #(.width(2)) multiplier_1 (.a(out_7), .b(out_10), .out(multiplier_1_out));  // open: cin, cout
  or or_2 (or_2_out, comparator_4_lt, comparator_4_gt);
  and and_3 (and_3_out, not_2_out, or_2_out);
  LED led_4 (.in(and_3_out));
  assign out_5 = {{1{adder_1_out[1]}}, adder_1_out};  // Bit_Extender bit_extender_1
  assign out_8 = {{1{subtractor_1_out[1]}}, subtractor_1_out};  // Bit_Extender bit_extender_2
  assign out_12 = {{1{multiplier_1_out[1]}}, multiplier_1_out};  // Bit_Extender bit_extender_3
  Multiplexer #(.enable("true"), .select(2), .width(3)) multiplexer_3 (
    .in0(out_5), .in1(out_8), .in2(out_12), .out(R), .sel(OP), .en(not_2_out));  // open: in3

  // Notes on the sheet:
  //   A
  //   B
  //   11 - X
  //   C
  //   T
  //   User Input
  //   10 - C
  //   00 - Soma
  //   01 -  Subtração
  //   10 - Multiplicação
  //   01 - B
  //   11 - X
  //   Guess number
  //   Inputs Inválidos
  //   ganhaste
  //   perdeste
endmodule
