// Logisim project 1Freq-PL1.circ as structural Verilog: 1 circuit, main circuit main
module main (
  input  A,
  input  B,
  input  C,
  input  D,
  output out_5
);

  wire nor_1_out, nor_2_out, nor_3_out, nor_4_out, nor_5_out, nor_6_out, nor_7_out, nor_8_out, nor_9_out,
       nor_10_out, nor_11_out, nor_12_out, nor_13_out, nor_14_out;

  nor nor_1 (nor_1_out, C, D);
  not nor_2 (nor_2_out, D);  // NOR_Gate
  not nor_3 (nor_3_out, B);  // NOR_Gate
  not nor_4 (nor_4_out, D);  // NOR_Gate
  not nor_5 (nor_5_out, C);  // NOR_Gate
  not nor_6 (nor_6_out, A);  // NOR_Gate
  not nor_7 (nor_7_out, C);  // NOR_Gate
  nor nor_8 (nor_8_out, nor_2_out, nor_3_out);
  nor nor_9 (nor_9_out, nor_4_out, nor_5_out);
  nor nor_10 (nor_10_out, B, nor_7_out);
  nor nor_11 (nor_11_out, C, nor_8_out);
  nor nor_12 (nor_12_out, nor_9_out, nor_6_out);
  nor nor_13 (nor_13_out, nor_10_out, nor_1_out);
  nor nor_14 (nor_14_out, nor_11_out, nor_12_out);
  nor nor_15 (out_5, nor_13_out, nor_14_out);
endmodule
