// Logisim project Exercicio2Jogadores4bits.circ as structural Verilog: 1 circuit, main circuit main
module main (
  input  in_1,
  input  [3:0] in_2,
  input  [3:0] in_3,
  input  [3:0] in_4,
  input  [3:0] in_5,
  input  [3:0] in_6,
  input  [3:0] in_7,
  input  V,
  input  [3:0] in_9,
  input  [3:0] in_10,
  output out_11,
  output out_12,
  output out_13,
  output out_14,
  output out_15,
  output out_16
);

  wire comparator_1_eq, comparator_2_eq, comparator_3_eq, comparator_4_eq, not_1_out, not_2_out, not_3_out,
       xor_1_out;

  Comparator #(.width(4)) comparator_1 (.a(in_2), .b(in_3), .eq(comparator_1_eq));  // open: gt, lt
  Comparator #(.width(4)) comparator_2 (.a(in_4), .b(in_5), .eq(comparator_2_eq));  // open: gt, lt
  Comparator #(.width(4)) comparator_3 (.a(in_6), .b(in_7), .eq(comparator_3_eq));  // open: gt, lt
  not not_1 (not_1_out, comparator_4_eq);
  not not_2 (not_2_out, comparator_3_eq);
  Comparator #(.width(4)) comparator_4 (.a(in_9), .b(in_10), .eq(comparator_4_eq));  // open: gt, lt
  Comparator #(.width(1)) comparator_5 (
    .a(comparator_1_eq), .b(comparator_2_eq), .gt(out_11), .eq(out_12), .lt(out_13));
  and and_1 (out_14, comparator_3_eq, not_1_out, V);
  and and_2 (out_16, V, not_2_out, comparator_4_eq);
  xor xor_1 (xor_1_out, comparator_3_eq, comparator_4_eq);
  not not_3 (not_3_out, xor_1_out);
  and and_3 (out_15, not_3_out, V);

  // Notes on the sheet:
  //   Nº P1
  //   Palpite P2
  //   Nº P2
  //   Palpite P1
  //   Nº P1
  //   Palpite P2
  //   Nº P2
  //   Palpite P1
  //   A
  //   B
  //   Player 1 ganha
  //   Empate
  //   Player 2 ganha
  //   Player 2 ganha
  //   Empate
  //   Player 1 ganha
endmodule
