// Logisim project ExercicioImpossiveisNAND_NOR.circ as structural Verilog: 1 circuit, main circuit main
module main (
  input  I0,
  input  I1,
  input  I0_2,
  input  S,
  input  D,
  input  I1_2,
  input  S_2,
  input  D_2,
  output out_9,
  output out_10
);

  wire nand_1_out, nand_2_out, nand_3_out, nand_4_out, nand_5_out, nand_6_out, nor_1_out, nor_2_out,
       nor_3_out, nor_4_out, nor_5_out;

  nand nand_1 (nand_1_out, I1_2, I1_2);
  nand nand_2 (nand_2_out, I0_2, I0_2);
  nand nand_3 (nand_3_out, I0_2, S_2);
  nand nand_4 (nand_4_out, nand_2_out, nand_1_out);
  nand nand_5 (nand_5_out, nand_4_out, nand_4_out);
  nand nand_6 (nand_6_out, nand_5_out, D_2);
  nand nand_7 (out_10, nand_6_out, nand_3_out);
  nor nor_1 (nor_1_out, I0, D);
  nor nor_2 (nor_2_out, I0, I0);
  nor nor_3 (nor_3_out, nor_2_out, S);
  nor nor_4 (nor_4_out, nor_3_out, I1);
  nor nor_5 (nor_5_out, nor_4_out, nor_4_out);
  nor nor_6 (out_9, nor_1_out, nor_5_out);

  // Notes on the sheet:
  //   Um elevador serve 3 pisos (P0, P1 e P2). O circuito de controle do motor de elevador dispõe de 2 sinais (S, D)
  //   que indicam o estado do motor (parado, subir e descer). Além disso, existem 2 indicadores (I0 e I1) que codificam em 
  //   binário o piso em que se encontra o elevador. Implemente o circuito de alarme de emergencia que indica a paragem
  //   do motor quando o elevador continua a descer e ja esta no piso mais baixo ou continua a subir e ja esta no piso mais alto
  //   Utilize apenas portas NAND de 2 entradas.
  //   Extraido por 1 para portas NAND
  //   Extraido por 0 para portas NOR
endmodule
