// Logisim project RandomNORCircuit.circ as structural Verilog: 1 circuit, main circuit main
module main (
  input  in_1,
  input  B,
  input  in_3,
  input  in_4,
  output out_5
);

  wire nor_1_out, nor_2_out, nor_3_out, nor_4_out, nor_5_out, nor_6_out, nor_7_out, nor_8_out, nor_9_out,
       nor_10_out;

  nor nor_1 (nor_1_out, in_1, in_4);
  nor nor_2 (nor_2_out, B, in_3);
  nor nor_3 (nor_3_out, in_4, in_4);
  nor nor_4 (nor_4_out, B, B);
  nor nor_5 (nor_5_out, in_1, in_3);
  nor nor_6 (nor_6_out, nor_1_out, B);
  nor nor_7 (nor_7_out, nor_2_out, nor_3_out);
  nor nor_8 (nor_8_out, nor_4_out, nor_5_out);
  nor nor_9 (nor_9_out, nor_7_out, nor_8_out);
  nor nor_10 (nor_10_out, nor_6_out, nor_9_out);
  nor nor_11 (out_5, nor_10_out, nor_10_out);

  // Notes on the sheet:
  //   A
  //   C
  //   D
endmodule
