// Logisim project class-01.circ as structural Verilog: 1 circuit, main circuit main
module main (
  input  Sensor_de_Chuva,
  input  S,
  input  \Ignição ,
  input  I,
  input  Comutador,
  input  C,
  input  S_2,
  input  C_2,
  input  I_2,
  output Parabrisas,
  output out_11,
  output out_12
);

  wire and_1_out, nand_1_out, nand_2_out, nand_3_out, nand_4_out, nand_6_out, nand_7_out;

  nand nand_1 (nand_1_out, S_2, S_2);
  nand nand_2 (nand_2_out, C_2, C_2);
  and and_1 (and_1_out, Sensor_de_Chuva, Sensor_de_Chuva, \Ignição , \Ignição );
  or or_1 (Parabrisas, and_1_out, and_1_out, Comutador, Comutador);
  nand nand_3 (nand_3_out, nand_1_out, nand_2_out);
  nand nand_4 (nand_4_out, nand_3_out, I_2);
  nand nand_5 (out_12, nand_4_out, nand_4_out);
  nand nand_6 (nand_6_out, S, I);
  nand nand_7 (nand_7_out, C, C);
  nand nand_8 (out_11, nand_6_out, nand_7_out);

  // Notes on the sheet:
  //   C + (I * S)
  //   !( !( I * !( !S * !C)))
  //   Ligar quando a ignição estiver ligada juntamente com o sensor de chuva ou o comutador estiver ligado
  //   !( !C * !( I * S)
endmodule
