// Logisim project class-02.circ as structural Verilog: 1 circuit, main circuit main
module main (
  input  A,
  input  B,
  input  C,
  input  D,
  output out_5
);

  wire nand_1_out, nand_2_out, nand_3_out, nand_4_out, nand_5_out, nand_6_out, nand_7_out;

  nand nand_1 (nand_1_out, B, B);
  nand nand_2 (nand_2_out, C, C);
  nand nand_3 (nand_3_out, B, D);
  nand nand_4 (nand_4_out, nand_1_out, nand_2_out);
  nand nand_5 (nand_5_out, nand_3_out, nand_3_out);
  nand nand_6 (nand_6_out, A, nand_4_out);
  nand nand_7 (nand_7_out, C, nand_5_out);
  nand nand_8 (out_5, nand_6_out, nand_7_out);

  // Notes on the sheet:
  //   Considere uma empresa com 4 sócios A, B, C, D com quotas de A = 40%, B = 30%, C = 20%, D = 10%. Nas assembleias as decisões são tomadas por uma maioria de 60%. Para controlar as votações, a empresa vai instalar um circuito em que cada sócio dispõe de um botão para votar. Implemente o circuito que permite determinar se uma decisão é aprovada usando apenas portas NAND.
endmodule
