// Logisim project (!ABC)+(A!BC)+(AB!C).circ as structural Verilog: 1 circuit, main circuit main
module main (
  input  A,
  input  B,
  input  C,
  output out_4
);

  wire nand_1_out, nand_2_out, nand_3_out, nand_4_out, nand_5_out, nand_6_out, nand_7_out, nand_8_out,
       nand_9_out, nand_10_out, nand_11_out, nand_12_out, nand_13_out, nand_14_out;

  not nand_1 (nand_1_out, A);  // NAND_Gate
  nand nand_2 (nand_2_out, C, B);
  not nand_3 (nand_3_out, B);  // NAND_Gate
  not nand_4 (nand_4_out, C);  // NAND_Gate
  not nand_5 (nand_5_out, nand_2_out);  // NAND_Gate
  nand nand_6 (nand_6_out, C, nand_3_out);
  nand nand_7 (nand_7_out, B, nand_4_out);
  not nand_8 (nand_8_out, nand_6_out);  // NAND_Gate
  not nand_9 (nand_9_out, nand_7_out);  // NAND_Gate
  nand nand_10 (nand_10_out, nand_1_out, nand_5_out);
  nand nand_11 (nand_11_out, A, nand_8_out);
  nand nand_12 (nand_12_out, A, nand_9_out);
  not nand_13 (nand_13_out, nand_14_out);  // NAND_Gate
  nand nand_14 (nand_14_out, nand_11_out, nand_12_out);
  nand nand_15 (out_4, nand_13_out, nand_10_out);
endmodule
