// Logisim project Teorica_9.circ as structural Verilog: 1 circuit, main circuit main
module main (
  input  in_1,
  input  E,
  input  R,
  input  E_2,
  input  D,
  output out_6,
  output out_7,
  output out_8
);

  wire nand_1_out, nand_2_out;

  nand nand_1 (nand_1_out, in_1, E);
  nand nand_2 (nand_2_out, E, R);
  D_Flip_Flop d_ff_1 (.D(E_2), .clk(D), .Q(out_8));  // open: Qn, preset, reset
  nand nand_3 (out_6, nand_1_out, out_7);
  nand nand_4 (out_7, out_6, nand_2_out);

  // Notes on the sheet:
  //   S
endmodule
